# Fritzing sketch reaction-game (saved by Fritzing 0.9.3b)
breadboards: 1

parts:
  Arduino_UNO = Arduino Uno (Rev3)
  LCD_16X2 = LCD screen
  R1 = Resistor [tolerance=±5% resistance=220 package=THT]
  RGB-LED = RGB LED (com. cathode, rgb) [package="5 mm [THT]"]
  R2 = Resistor [tolerance=±5% resistance=220 package=THT]
  BTN_PL1_BLUE = Pushbutton [package=THT]
  BTN_PL2_RED = Pushbutton [package=THT]
  BTN_PL2_GREEN = Pushbutton [package=THT]
  BTN_PL2_BLUE = Pushbutton [package=THT]
  BTN_PL1_RED = Pushbutton [package=THT]
  BTN_PL1_GREEN = Pushbutton [package=THT]
  D1 = Rectifier Diode [part_number=1N4001 package="300 mil [THT]"]
  D2 = Rectifier Diode [part_number=1N4001 package="300 mil [THT]"]
  D3 = Rectifier Diode [part_number=1N4001 package="300 mil [THT]"]
  D4 = Rectifier Diode [part_number=1N4001 package="300 mil [THT]"]
  D6 = Rectifier Diode [part_number=1N4001 package="300 mil [THT]"]
  D5 = Rectifier Diode [part_number=1N4001 package="300 mil [THT]"]

nets:
  N1: Arduino_UNO.A0, LCD_16X2.RS
  N2: Arduino_UNO.A1, LCD_16X2.E
  N3: Arduino_UNO.A2, LCD_16X2.DB4
  N4: Arduino_UNO.A3, LCD_16X2.DB5
  N5: Arduino_UNO.A4/SDA, LCD_16X2.DB6
  N6: Arduino_UNO.D8, BTN_PL2_RED.leg0, D3.anode
  N7: Arduino_UNO.D9_PWM, BTN_PL2_GREEN.leg0, D5.anode
  N8: Arduino_UNO.D10_PWM/SS, BTN_PL2_BLUE.leg0, D6.anode
  N9: Arduino_UNO.D11_PWM/MOSI, RGB-LED.red_anode
  N10: Arduino_UNO.D12/MISO, RGB-LED.blue_anode
  N11: Arduino_UNO.D13/SCK, RGB-LED.green_anode
  GND: Arduino_UNO.GND, LCD_16X2.VSS, LCD_16X2.V0, LCD_16X2.R/W, LCD_16X2.LED-, R2.Pin_1, BTN_PL1_BLUE.leg1, BTN_PL2_RED.leg1, BTN_PL2_GREEN.leg1, BTN_PL2_BLUE.leg1, BTN_PL1_RED.leg1, BTN_PL1_GREEN.leg1
  N12: Arduino_UNO.A5/SCL, LCD_16X2.DB7
  N13: Arduino_UNO.D3_PWM, D1.cathode, D2.cathode, D3.cathode, D4.cathode, D6.cathode, D5.cathode
  N14: Arduino_UNO.D5_PWM, BTN_PL1_RED.leg0, D1.anode
  N15: Arduino_UNO.D6_PWM, BTN_PL1_GREEN.leg0, D2.anode
  N16: Arduino_UNO.D7, BTN_PL1_BLUE.leg0, D4.anode
  5V: Arduino_UNO.5V, LCD_16X2.VDD, R1.Pin_1
  N17: LCD_16X2.LED+, R1.Pin_0
  N18: RGB-LED.common_cathode, R2.Pin_0
